# Fritzing sketch water-quality-sensors-wiring-diagram (saved by Fritzing 0.9.3b)
breadboards: 1

parts:
  BLE_Nano_v2 = Bluetooth Module Breakout - Roving Networks (RN-41)
  Conductivity_Circuit1 = Conductivity Circuit
  The_Things_Uno = Arduino Leonardo (Rev3b)
  Pre-Assembled_Female_BNC1 = Pre-Assembled Female BNC

nets:
  VCC: BLE_Nano_v2.VCC, Conductivity_Circuit1.Vcc, The_Things_Uno.3V3, Pre-Assembled_Female_BNC1.NC
  GND: BLE_Nano_v2.GND, Conductivity_Circuit1.GND#0, The_Things_Uno.GND
  N1: BLE_Nano_v2.UARTRX, Conductivity_Circuit1.TX, The_Things_Uno.D10_PWM/A10
  N2: Conductivity_Circuit1.RX, The_Things_Uno.D11_PWM
  N3: Conductivity_Circuit1.PRB, Pre-Assembled_Female_BNC1.PRB
  N4: Conductivity_Circuit1.GND#5, Pre-Assembled_Female_BNC1.GND
